// Logisim project Guia06.circ as structural Verilog: 1 circuit, main circuit Guia0605
module Guia0605 (
  input  x,
  input  y,
  input  z,
  output o1,
  output o2
);

  wire and_1_out, and_2_out, and_3_out, and_4_out, and_5_out, not_1_out, not_2_out, not_3_out, not_4_out,
       not_5_out, not_6_out, not_7_out, not_8_out, or_1_out, or_2_out;

  not not_1 (not_1_out, y);
  not not_2 (not_2_out, z);
  not not_3 (not_3_out, y);
  not not_4 (not_4_out, x);
  and and_1 (and_1_out, z, y);
  not not_5 (not_5_out, x);
  and and_2 (and_2_out, x, not_1_out);
  and and_3 (and_3_out, x, not_2_out);
  or or_1 (or_1_out, not_3_out, not_4_out);
  not not_6 (not_6_out, or_1_out);
  and and_4 (and_4_out, y, x);
  not not_7 (not_7_out, and_4_out);
  not not_8 (not_8_out, or_2_out);
  or or_2 (or_2_out, and_1_out, not_5_out);
  or or_3 (o2, and_2_out, and_3_out);
  and and_5 (and_5_out, not_6_out, not_7_out);
  or or_4 (o1, and_5_out, not_8_out);

  // Notes on the sheet:
  //   circuito nao otimizado
  //   circuito otimizado
endmodule
