// Logisim project Circuitos.circ as structural Verilog: 1 circuit, main circuit main
module main (
  input  pulse,
  input  In,
  input  CLR,
  input  pulse_2,
  input  In_2,
  input  CLR_2,
  input  pulse_3,
  input  In_3,
  input  CLR_3,
  input  pulse_4,
  input  In_4,
  input  Preset,
  input  CLK,
  input  In_5,
  input  CLR_4,
  input  CLK_2,
  input  CLR_5,
  input  CLK_3,
  input  CLR_6
);

  wire and_1_out, and_2_out, and_3_out, and_4_out, j_k_ff_3_qn, j_k_ff_4_qn, j_k_ff_6_q, j_k_ff_7_qn,
       j_k_ff_8_qn, j_k_ff_14_q, j_k_ff_15_qn, j_k_ff_16_qn, j_k_ff_20_q, j_k_ff_22_qn, j_k_ff_26_q,
       j_k_ff_28_qn, not_1_out, not_2_out, not_3_out, not_4_out, not_5_out, not_6_out, not_7_out, not_8_out,
       not_9_out, not_10_out, not_11_out, not_12_out, not_13_out, not_14_out, or_1_out, or_2_out, or_3_out;
  wire [2:0] t_ff_1_q;
  wire [3:0] j_k_ff_3_q, j_k_ff_4_q;
  wire [4:0] j_k_ff_9_q, j_k_ff_10_q, j_k_ff_25_qn, j_k_ff_26_qn;

  or or_1 (or_1_out, CLR_3, and_1_out);
  and and_1 (and_1_out, not_1_out, j_k_ff_3_q[1], not_2_out, j_k_ff_3_q[3]);
  or or_2 (or_2_out, Preset, and_2_out);
  and and_2 (and_2_out, not_3_out, j_k_ff_8_qn, not_4_out, j_k_ff_22_qn);
  or or_3 (or_3_out, CLR_4, and_3_out);
  // Probe on j_k_ff_25_qn[4]
  J_K_Flip_Flop j_k_ff_1 (.J(In), .clk(j_k_ff_25_qn[3]), .K(In), .Qn(j_k_ff_25_qn[4]), .reset(CLR));  // open: Q, preset
  // Probe on j_k_ff_26_qn[4]
  J_K_Flip_Flop j_k_ff_2 (
    .J(In_2), .clk(j_k_ff_6_q), .K(In_2), .Qn(j_k_ff_26_qn[4]), .reset(CLR_2));  // open: Q, preset
  // Probe on j_k_ff_3_q[3]
  J_K_Flip_Flop j_k_ff_3 (
    .J(In_3), .clk(pulse_3), .K(In_3), .Q(j_k_ff_3_q[0]), .Qn(j_k_ff_3_qn), .reset(or_1_out));  // open: preset
  not not_1 (not_1_out, j_k_ff_3_q[0]);
  not not_2 (not_2_out, j_k_ff_3_q[2]);
  // Probe on j_k_ff_4_q[3]
  J_K_Flip_Flop j_k_ff_4 (
    .J(In_4), .clk(pulse_4), .K(In_4), .Q(j_k_ff_4_q[0]), .Qn(j_k_ff_4_qn), .preset(or_2_out));  // open: reset
  not not_3 (not_3_out, j_k_ff_4_qn);
  not not_4 (not_4_out, j_k_ff_16_qn);
  // Probe on t_ff_1_q[0]
  T_Flip_Flop t_ff_1 (.clk(CLK), .T(In_5), .Q(t_ff_1_q[0]), .reset(or_3_out));  // open: Qn, preset
  and and_3 (and_3_out, t_ff_1_q[0], t_ff_1_q[1], t_ff_1_q[2]);
  not not_5 (not_5_out, j_k_ff_9_q[4]);
  not not_6 (not_6_out, j_k_ff_28_qn);
  // Probe on j_k_ff_25_qn[3]
  J_K_Flip_Flop j_k_ff_5 (.J(In), .clk(j_k_ff_25_qn[2]), .K(In), .Qn(j_k_ff_25_qn[3]), .reset(CLR));  // open: Q, preset
  // Probe on j_k_ff_26_qn[3]
  J_K_Flip_Flop j_k_ff_6 (
    .J(In_2), .clk(j_k_ff_14_q), .K(In_2), .Q(j_k_ff_6_q), .Qn(j_k_ff_26_qn[3]), .reset(CLR_2));  // open: preset
  // Probe on j_k_ff_3_q[2]
  J_K_Flip_Flop j_k_ff_7 (
    .J(In_3), .clk(j_k_ff_3_qn), .K(In_3), .Q(j_k_ff_3_q[1]), .Qn(j_k_ff_7_qn), .reset(or_1_out));  // open: preset
  J_K_Flip_Flop j_k_ff_8 (
    .J(In_4), .clk(j_k_ff_4_q[0]), .K(In_4), .Q(j_k_ff_4_q[1]), .Qn(j_k_ff_8_qn), .preset(or_2_out));  // open: reset
  T_Flip_Flop t_ff_2 (.clk(CLK), .T(t_ff_1_q[0]), .Q(t_ff_1_q[1]), .reset(or_3_out));  // open: Qn, preset
  // Probe on j_k_ff_9_q[0]
  J_K_Flip_Flop #(.Pre_Clr_Positions("BELOW_ABOVE")) j_k_ff_9 (
    .J(j_k_ff_9_q[4]), .clk(CLK_2), .K(not_5_out), .Q(j_k_ff_9_q[0]), .preset(CLR_5));  // open: Qn, reset
  not not_7 (not_7_out, j_k_ff_9_q[0]);
  // Probe on j_k_ff_10_q[0]
  J_K_Flip_Flop #(.Pre_Clr_Positions("BELOW_ABOVE")) j_k_ff_10 (
    .J(j_k_ff_28_qn), .clk(CLK_3), .K(not_6_out), .Q(j_k_ff_10_q[0]), .preset(CLR_6));  // open: Qn, reset
  not not_8 (not_8_out, j_k_ff_10_q[0]);
  // Probe on j_k_ff_4_q[2]
  // Probe on t_ff_1_q[1]
  and and_4 (and_4_out, t_ff_1_q[1], t_ff_1_q[0]);
  // Probe on j_k_ff_9_q[1]
  J_K_Flip_Flop j_k_ff_11 (
    .J(j_k_ff_9_q[0]), .clk(CLK_2), .K(not_7_out), .Q(j_k_ff_9_q[1]), .reset(CLR_5));  // open: Qn, preset
  not not_9 (not_9_out, j_k_ff_9_q[1]);
  // Probe on j_k_ff_10_q[1]
  J_K_Flip_Flop j_k_ff_12 (
    .J(j_k_ff_10_q[0]), .clk(CLK_3), .K(not_8_out), .Q(j_k_ff_10_q[1]), .reset(CLR_6));  // open: Qn, preset
  not not_10 (not_10_out, j_k_ff_10_q[1]);
  // Probe on j_k_ff_25_qn[2]
  J_K_Flip_Flop j_k_ff_13 (
    .J(In), .clk(j_k_ff_25_qn[1]), .K(In), .Qn(j_k_ff_25_qn[2]), .reset(CLR));  // open: Q, preset
  // Probe on j_k_ff_26_qn[2]
  J_K_Flip_Flop j_k_ff_14 (
    .J(In_2), .clk(j_k_ff_20_q), .K(In_2), .Q(j_k_ff_14_q), .Qn(j_k_ff_26_qn[2]), .reset(CLR_2));  // open: preset
  // Probe on j_k_ff_3_q[1]
  J_K_Flip_Flop j_k_ff_15 (
    .J(In_3), .clk(j_k_ff_7_qn), .K(In_3), .Q(j_k_ff_3_q[2]), .Qn(j_k_ff_15_qn), .reset(or_1_out));  // open: preset
  // Probe on j_k_ff_4_q[1]
  J_K_Flip_Flop j_k_ff_16 (
    .J(In_4), .clk(j_k_ff_4_q[1]), .K(In_4), .Q(j_k_ff_4_q[2]), .Qn(j_k_ff_16_qn), .preset(or_2_out));  // open: reset
  // Probe on t_ff_1_q[2]
  T_Flip_Flop t_ff_3 (.clk(CLK), .T(and_4_out), .Q(t_ff_1_q[2]), .reset(or_3_out));  // open: Qn, preset
  // Probe on j_k_ff_9_q[2]
  J_K_Flip_Flop j_k_ff_17 (
    .J(j_k_ff_9_q[1]), .clk(CLK_2), .K(not_9_out), .Q(j_k_ff_9_q[2]), .reset(CLR_5));  // open: Qn, preset
  // Probe on j_k_ff_10_q[2]
  J_K_Flip_Flop j_k_ff_18 (
    .J(j_k_ff_10_q[1]), .clk(CLK_3), .K(not_10_out), .Q(j_k_ff_10_q[2]), .reset(CLR_6));  // open: Qn, preset
  // Probe on j_k_ff_25_qn[1]
  J_K_Flip_Flop j_k_ff_19 (
    .J(In), .clk(j_k_ff_25_qn[0]), .K(In), .Qn(j_k_ff_25_qn[1]), .reset(CLR));  // open: Q, preset
  // Probe on j_k_ff_26_qn[1]
  J_K_Flip_Flop j_k_ff_20 (
    .J(In_2), .clk(j_k_ff_26_q), .K(In_2), .Q(j_k_ff_20_q), .Qn(j_k_ff_26_qn[1]), .reset(CLR_2));  // open: preset
  // Probe on j_k_ff_3_q[0]
  J_K_Flip_Flop j_k_ff_21 (
    .J(In_3), .clk(j_k_ff_15_qn), .K(In_3), .Q(j_k_ff_3_q[3]), .reset(or_1_out));  // open: Qn, preset
  // Probe on j_k_ff_4_q[0]
  J_K_Flip_Flop j_k_ff_22 (
    .J(In_4), .clk(j_k_ff_4_q[2]), .K(In_4), .Q(j_k_ff_4_q[3]), .Qn(j_k_ff_22_qn), .preset(or_2_out));  // open: reset
  // Probe on t_ff_1_q
  // Probe on t_ff_1_q
  J_K_Flip_Flop j_k_ff_23 (
    .J(j_k_ff_9_q[2]), .clk(CLK_2), .K(not_11_out), .Q(j_k_ff_9_q[3]), .reset(CLR_5));  // open: Qn, preset
  not not_11 (not_11_out, j_k_ff_9_q[2]);
  J_K_Flip_Flop j_k_ff_24 (
    .J(j_k_ff_10_q[2]), .clk(CLK_3), .K(not_12_out), .Q(j_k_ff_10_q[3]), .reset(CLR_6));  // open: Qn, preset
  not not_12 (not_12_out, j_k_ff_10_q[2]);
  // Probe on j_k_ff_25_qn[0]
  J_K_Flip_Flop j_k_ff_25 (.J(In), .clk(pulse), .K(In), .Qn(j_k_ff_25_qn[0]), .reset(CLR));  // open: Q, preset
  // Probe on j_k_ff_26_qn[0]
  J_K_Flip_Flop j_k_ff_26 (
    .J(In_2), .clk(pulse_2), .K(In_2), .Q(j_k_ff_26_q), .Qn(j_k_ff_26_qn[0]), .reset(CLR_2));  // open: preset
  // Probe on j_k_ff_3_q
  // Probe on j_k_ff_4_q
  // Probe on j_k_ff_9_q[3]
  not not_13 (not_13_out, j_k_ff_9_q[3]);
  // Probe on j_k_ff_10_q[3]
  not not_14 (not_14_out, j_k_ff_10_q[3]);
  // Probe on j_k_ff_25_qn
  // Probe on j_k_ff_26_qn
  // Probe on j_k_ff_9_q[4]
  J_K_Flip_Flop j_k_ff_27 (
    .J(j_k_ff_9_q[3]), .clk(CLK_2), .K(not_13_out), .Q(j_k_ff_9_q[4]), .reset(CLR_5));  // open: Qn, preset
  // Probe on j_k_ff_10_q[4]
  J_K_Flip_Flop j_k_ff_28 (
    .J(j_k_ff_10_q[3]), .clk(CLK_3), .K(not_14_out), .Q(j_k_ff_10_q[4]), .Qn(j_k_ff_28_qn), .reset(CLR_6));  // open: preset
  // Probe on j_k_ff_9_q
  // Probe on j_k_ff_10_q

  // Notes on the sheet:
  //   Matrícula: 723185
  //   Aluna: Danielle Dias Vieira
  //   Exercício 01 - Contador Assíncrono decrescente com 5 bits de comprimento
  //   Exercício 02 - Contador Assíncrono crescente com 5 bits de comprimento
  //   Exercício 03 - Contador Assíncrono Decádico crescente com 4 bits de comprimento
  //   Exercício 04 - Contador Assíncrono Decádico decrescente
  //   Exercício 05 - Contador Síncrono módulo 7
  //   Exercício 06 - Contador em anel com 5 bits de comprimento
  //   Exercício 07 - Contador em anel torcido com 5 bits de comprimento
endmodule
